# Fritzing sketch Schematic (saved by Fritzing 0.9.3b)
breadboards: 1

parts:
  SG3 = Buzzer 12mm [package=buzzer-12mm-ns]  # not connected
  Part1 = Arduino Uno (Rev3) - ICSP
  Part2 = Arduino Uno (Rev3) - ICSP  # not connected
  LED1 = LEDs [package=led10mm]
  R1 = Resistor [tolerance=±5% resistance=220 package="0603 [SMD]"]

nets:
  N1: Part1.D2, R1.Pin_0
  N2: Part1.GND, LED1.C, LED1.A, R1.Pin_1
